# Fritzing sketch Hardware1 Reloj (saved by Fritzing 0.9.10b)
breadboards: 3

parts:
  Tiny_RTC1 = Tiny RTC
  Componente1 = Arduino Nano (Rev3.0) (ICSP)
  LCM1602_IIC1 = LCM1602 IIC [part_number="LCM1602 IIC" chip_label="LCM1602 IIC" package="DIP (Dual Inline) [THT]"]
  U1 = LCD-16X2 [package=lcd-16x2_noholes]
  R1 = Resistor [tolerance=±5% power=0.25 resistance=10k package=THT]
  R2 = Resistor [tolerance=±5% power=0.25 resistance=10k package=THT]
  R3 = Resistor [tolerance=±5% power=0.25 resistance=10k package=THT]
  R4 = Resistor [tolerance=±5% power=0.25 resistance=10k package=THT]
  R5 = Resistor [tolerance=±5% power=0.25 resistance=10k package=THT]
  R6 = Resistor [tolerance=±5% power=0.25 resistance=10k package=THT]
  S1 = Pushbutton [package="[THT]"]
  S2 = Pushbutton [package="[THT]"]
  S3 = Pushbutton [package="[THT]"]
  S4 = Pushbutton [package="[THT]"]
  S5 = Pushbutton [package="[THT]"]
  S6 = Pushbutton [package="[THT]"]
  DHT1 = DHT11 Humitidy and Temperature Sensor
  J1 = Piezo Speaker

nets:
  N1: Tiny_RTC1.SCL, Componente1.A5, LCM1602_IIC1.SCL
  N2: Tiny_RTC1.SDA, LCM1602_IIC1.SDA
  VCC: Tiny_RTC1.VCC, Componente1.VIN, LCM1602_IIC1.VCC, R1.Pin_0, R2.Pin_0, R3.Pin_0, R4.Pin_0, R5.Pin_0, R6.Pin_0, DHT1.VDD
  GND: Tiny_RTC1.GND, Componente1.D7, Componente1.D8, Componente1.D9, Componente1.D10, Componente1.D11/MOSI, Componente1.D12/MISO, Componente1.GND, LCM1602_IIC1.GND, R1.Pin_1, R2.Pin_1, R3.Pin_1, R4.Pin_1, R5.Pin_1, R6.Pin_1, S1.Pin_3, S1.Pin_4, S2.Pin_3, S2.Pin_4, S3.Pin_3, S3.Pin_4, S4.Pin_3, S4.Pin_4, S5.Pin_3, S5.Pin_4, S6.Pin_3, S6.Pin_4, DHT1.GND, J1.pin1
  N3: Componente1.D3, J1.pin2
  N4: Componente1.D5, DHT1.DATA
  VSS: LCM1602_IIC1.VSS, U1.VSS
  VDD: LCM1602_IIC1.VDD, U1.VDD
  N5: LCM1602_IIC1.V0, U1.VO
  N6: LCM1602_IIC1.RS, U1.RS
  N7: LCM1602_IIC1.RW, U1.R_W
  N8: LCM1602_IIC1.E, U1.E
  N9: LCM1602_IIC1.D0, U1.DB0
  N10: LCM1602_IIC1.D1, U1.DB1
  N11: LCM1602_IIC1.D2, U1.DB2
  N12: LCM1602_IIC1.D3, U1.DB3
  N13: LCM1602_IIC1.D4, U1.DB4
  N14: LCM1602_IIC1.D5, U1.DB5
  N15: LCM1602_IIC1.D6, U1.DB6
  N16: LCM1602_IIC1.D7, U1.DB7
  N17: LCM1602_IIC1.A, U1.A
  N18: LCM1602_IIC1.K, U1.K
  N19: LCM1602_IIC1.LED_A, LCM1602_IIC1.LED_B

custom parts:
  Tiny RTC: Tiny RTC I2C module DS1370Z RTC and AT24C32 EEPROM
  LCM1602 IIC: I2C-Module to use a 1602 or 2004 LCD on with the wire.h libory Serial LCD Modul
  DHT11 Humitidy and Temperature Sensor: DHT11 Humidity and Temperature Sensor
